# Fritzing sketch 3digit7segment (saved by Fritzing 0.8.3b)
breadboards: 1

parts:
  U1 = 7-SEGMENT-4DIGIT-YOUNGSUN [package=7-segment-4digit-youngsun-longpads]  # not connected
  R1 = Resistor [tolerance=±1% resistance=200 package=THT]
  R2 = Resistor [tolerance=±1% resistance=200 package=THT]
  R3 = Resistor [tolerance=±1% resistance=200 package=THT]
  R4 = Resistor [tolerance=±1% resistance=200 package=THT]
  R5 = Resistor [tolerance=±1% resistance=200 package=THT]
  Part1 = Arduino Uno (Rev3)
  R6 = Resistor [tolerance=±1% resistance=200 package=THT]
  R7 = Resistor [tolerance=±1% resistance=200 package=THT]
  R8 = Resistor [tolerance=±1% resistance=200 package=THT]

nets:
  N1: R1.Pin_0, Part1.ICSP_SCK, Part1.D13/SCK
  N2: R2.Pin_0, Part1.ICSP_MISO, Part1.D12/MISO
  N3: R3.Pin_0, Part1.ICSP_MOSI, Part1.D11_PWM/MOSI
  N4: R4.Pin_0, Part1.D10_PWM/SS
  N5: R5.Pin_0, Part1.D9_PWM
  N6: Part1.D8, R6.Pin_0
  N7: Part1.D6_PWM, R8.Pin_0
  N8: Part1.D7, R7.Pin_0
