# Fritzing sketch ldr-analog (saved by Fritzing 0.8.3b)
circuit board: 6.88561cm x 5.36311cm
breadboards: 1

parts:
  R5 = Photocell (LDR) [package=THT]
  Arduino1 = Arduino Uno (Rev3)
  LED3 = LED - 5mm [color="Red (633nm)" package="5 mm [THT]"]
  R6 = Resistor [tolerance=±5% resistance=10k package=THT]

nets:
  N1: R5.pin_0, Arduino1.5V
  N2: R5.pin_1, Arduino1.A2, R6.Pin_0
  N3: Arduino1.ICSP_SCK, Arduino1.D13/SCK, LED3.cathode
  N4: Arduino1.GND, LED3.anode, R6.Pin_1

notes:
  In this example, photocell values are read in through an 'Analog In' pin. The values are then used to control the blinking rate of an LED.
  Using a multimeter, check the min and max resistance of the photocell in different light conditions. Then calculate the resistor's value with the Axel-Benz formula: Rref = sqrt(Rmin*Rmax)
  Related example: http://www.ladyada.net/learn/sensors/cds.html
