# Fritzing sketch ldr (saved by Fritzing 0.8.3b)
breadboards: 1

parts:
  R1 = Resistor [tolerance=±5% resistance=10k package=THT]
  VCC1 = Battery block 9V
  LDR = Photocell (LDR) [package=THT]

nets:
  Vout: R1.Pin_0, LDR.pin_1
  N1: R1.Pin_1, VCC1.+
  N2: VCC1.-, LDR.pin_0
