# Fritzing sketch reflective-optical-sensor (saved by Fritzing 0.8.3b)
breadboards: 1

parts:
  Reflective_Optical_Sensor = PHOTOTRANSISTOR REFLECTIVE OBJECT SENSOR [package=qrb1114-side]
  R1 = Resistor [tolerance=±5% resistance=560 package=THT]
  R2 = Resistor [tolerance=±5% resistance=10k package=THT]
  Arduino = Arduino Uno (Rev3)

nets:
  N1: Reflective_Optical_Sensor.A, Reflective_Optical_Sensor.C, Arduino.5V
  N2: Reflective_Optical_Sensor.E, R2.Pin_0, Arduino.A0
  N3: Reflective_Optical_Sensor.K, R1.Pin_0
  N4: R1.Pin_1, R2.Pin_1, Arduino.GND
