# Fritzing sketch reflexo (saved by Fritzing 0.8.3b)
breadboards: 1

parts:
  ARD1 = Arduino Uno (Rev3)
  S1 = Pushbutton [package="[THT]"]
  S2 = Pushbutton [package="[THT]"]
  R1 = Resistor [tolerance=±5% resistance=330 package=THT]
  LED1 = LED - 5mm [color="Yellow (592nm)" package="5 mm [THT]"]
  R2 = Resistor [tolerance=±5% resistance=330 package=THT]
  R3 = Resistor [tolerance=±5% resistance=330 package=THT]
  LED2 = LED - 5mm [color="Blue (470nm)" package="5 mm [THT]"]
  LED4 = LED - 5mm [color="Red (633nm)" package="5 mm [THT]"]

nets:
  N1: ARD1.ICSP_MISO, ARD1.D12/MISO, R2.Pin_1
  N2: ARD1.GND, R1.Pin_0, R3.Pin_0, LED2.cathode
  N3: ARD1.D11_PWM/MOSI, LED1.anode
  N4: ARD1.D13/SCK, S1.Pin_1, S1.Pin_2
  N5: ARD1.D0/RX, S2.Pin_3, S2.Pin_4
  N6: ARD1.D1/TX, LED4.anode
  N7: ARD1.5V, S1.Pin_3, S1.Pin_4, S2.Pin_1, S2.Pin_2
  N8: R1.Pin_1, LED1.cathode
  N9: R2.Pin_0, LED2.anode
  N10: R3.Pin_1, LED4.cathode
