# Fritzing sketch semaforo (saved by Fritzing 0.8.3b)
breadboards: 1

parts:
  Arduino = Arduino Uno (Rev3)
  LED3 = LED - 5mm [color="Green (565nm)" package="5 mm [THT]"]
  LED2 = LED - 5mm [color="Yellow (595nm)" package="5 mm [THT]"]
  LED1 = LED - 5mm [color="Red (633nm)" package="5 mm [THT]"]
  R1 = Resistor [tolerance=±5% resistance=1k package=THT]
  R3 = Resistor [tolerance=±5% resistance=1k package=THT]
  R2 = Resistor [tolerance=±5% resistance=1k package=THT]
  R4 = Resistor [tolerance=±5% resistance=1k package=THT]
  R5 = Rotary Potentiometer (Large) [package=THT]  # not connected

nets:
  N1: Arduino.GND, R1.Pin_0, R3.Pin_0, R2.Pin_0, R4.Pin_0
  N2: Arduino.D2, LED1.anode
  N3: Arduino.D3_PWM, LED2.anode
  N4: Arduino.D4, LED3.anode
  N5: LED3.cathode, R3.Pin_1, R4.Pin_1
  N6: LED2.cathode, R2.Pin_1
  N7: LED1.cathode, R1.Pin_1
