# Fritzing sketch semaforo2 (saved by Fritzing 0.8.3b)
breadboards: 1

parts:
  Arduino = Arduino Uno (Rev3)
  LED3 = LED - 5mm [color="Green (565nm)" package="5 mm [THT]"]
  LED2 = LED - 5mm [color="Yellow (595nm)" package="5 mm [THT]"]
  LED1 = LED - 5mm [color="Red (633nm)" package="5 mm [THT]"]
  R1 = Resistor [tolerance=±5% resistance=1k package=THT]
  R3 = Resistor [tolerance=±5% resistance=1k package=THT]
  R2 = Resistor [tolerance=±5% resistance=1k package=THT]
  R4 = Resistor [tolerance=±5% resistance=1k package=THT]
  R5 = Resistor [tolerance=±5% resistance=1k package=THT]
  R6 = Photocell (LDR) [package=THT]

nets:
  N1: Arduino.A0, R5.Pin_0, R6.pin_0
  N2: Arduino.GND, R1.Pin_0, R3.Pin_0, R2.Pin_0, R4.Pin_0, R6.pin_1
  N3: Arduino.D2, LED1.anode
  N4: Arduino.D3_PWM, LED2.anode
  N5: Arduino.D4, LED3.anode
  N6: Arduino.5V, R5.Pin_1
  N7: LED3.cathode, R3.Pin_1, R4.Pin_1
  N8: LED2.cathode, R2.Pin_1
  N9: LED1.cathode, R1.Pin_1
