# Fritzing sketch servo (saved by Fritzing 0.8.3b)
breadboards: 1

parts:
  VCC1 = 4 x AAA Battery Mount
  Part1 = Arduino Uno (Rev3)
  J1 = Basic Servo

nets:
  N1: VCC1.-, Part1.GND
  N2: Part1.D9_PWM, J1.pulse
